# Fritzing sketch Schematics (saved by Fritzing 1.0.2b)
breadboards: 1

parts:
  LED1 = LED - 5mm [color="Red (633nm)" current=0.030A package="5 mm [THT]"]
  Part1 = Arduino Uno (Rev3)
  KY-1 = Keyes Relay [package=THT]
  HC-SR04_Sensor_1 = HC-SR04 Ultrasonic Distance Sensor
  HC-SR04_Sensor_2 = HC-SR04 Ultrasonic Distance Sensor

nets:
  N1: LED1.cathode, KY-1.C
  N2: LED1.anode, KY-1.NC, KY-1.NO
  GND: Part1.GND, KY-1.ground, HC-SR04_Sensor_1.GND, HC-SR04_Sensor_2.GND
  N3: Part1.D2, HC-SR04_Sensor_1.TRIG
  N4: Part1.D3_PWM, HC-SR04_Sensor_1.ECHO
  N5: Part1.D5_PWM, KY-1.power
  N6: Part1.D6_PWM, HC-SR04_Sensor_2.TRIG
  N7: Part1.D7, HC-SR04_Sensor_2.ECHO
  VCC: Part1.5V, KY-1.signal, HC-SR04_Sensor_1.VCC, HC-SR04_Sensor_2.VCC

notes:
  Distance Sensor 2 (Top Sensor)
  Distance Sensor 1 (Bottom Sensor)
  Relay
  Light

custom parts:
  Keyes Relay: The Keyes 5V relay module is suitable for SCM development, home appliance control. It uses a 5V~12V TIL control signal which can control DC / AC signal.
